// Logisim project Processor.circ as structural Verilog: 18 circuits, main circuit main
module main (
  input  [19:0] in_1,
  input  in_2,
  input  in_3,
  output [19:0] out_4
);

  Register register_1 (.Input(in_1), .clk(in_2), .select(in_3), .out_4(out_4));
endmodule

module D_Latch (
  input  D,
  input  clk,
  output \output 
);

  wire and_1_out, and_2_out, nor_1_out, not_1_out;

  not not_1 (not_1_out, D);
  and and_1 (and_1_out, D, clk);
  and and_2 (and_2_out, clk, not_1_out);
  nor nor_1 (nor_1_out, and_1_out, \output );
  nor nor_2 (\output , nor_1_out, and_2_out);
endmodule

module DFF (
  input  clk,
  input  D,
  output \output 
);

  wire d_latch_1_output, not_1_out;

  D_Latch d_latch_1 (.D(D), .clk(not_1_out), .\output (d_latch_1_output));
  not not_1 (not_1_out, clk);
  D_Latch d_latch_2 (.D(d_latch_1_output), .clk(clk), .\output (\output ));
endmodule

module Register (
  input  [19:0] Input,
  input  clk,
  input  select,
  output [19:0] out_4
);

  wire multiplexer_1_out, multiplexer_2_out, multiplexer_3_out, multiplexer_4_out, multiplexer_5_out,
       multiplexer_6_out, multiplexer_7_out, multiplexer_8_out, multiplexer_9_out, multiplexer_10_out,
       multiplexer_11_out, multiplexer_12_out, multiplexer_13_out, multiplexer_14_out, multiplexer_15_out,
       multiplexer_16_out, multiplexer_17_out, multiplexer_18_out, multiplexer_19_out, multiplexer_20_out,
       not_1_out;

  not not_1 (not_1_out, select);
  Multiplexer #(.enable("false")) multiplexer_1 (
    .in0(Input[19]), .in1(out_4[19]), .out(multiplexer_1_out), .sel(not_1_out));
  DFF dff_1 (.clk(clk), .D(multiplexer_1_out), .\output (out_4[19]));
  Multiplexer #(.enable("false")) multiplexer_2 (
    .in0(Input[17]), .in1(out_4[17]), .out(multiplexer_2_out), .sel(not_1_out));
  Multiplexer #(.enable("false")) multiplexer_3 (
    .in0(Input[18]), .in1(out_4[18]), .out(multiplexer_3_out), .sel(not_1_out));
  DFF dff_2 (.clk(clk), .D(multiplexer_3_out), .\output (out_4[18]));
  Multiplexer #(.enable("false")) multiplexer_4 (
    .in0(Input[16]), .in1(out_4[16]), .out(multiplexer_4_out), .sel(not_1_out));
  DFF dff_3 (.clk(clk), .D(multiplexer_4_out), .\output (out_4[16]));
  DFF dff_4 (.clk(clk), .D(multiplexer_2_out), .\output (out_4[17]));
  Multiplexer #(.enable("false")) multiplexer_5 (
    .in0(Input[15]), .in1(out_4[15]), .out(multiplexer_5_out), .sel(not_1_out));
  DFF dff_5 (.clk(clk), .D(multiplexer_5_out), .\output (out_4[15]));
  Multiplexer #(.enable("false")) multiplexer_6 (
    .in0(Input[14]), .in1(out_4[14]), .out(multiplexer_6_out), .sel(not_1_out));
  DFF dff_6 (.clk(clk), .D(multiplexer_6_out), .\output (out_4[14]));
  Multiplexer #(.enable("false")) multiplexer_7 (
    .in0(Input[13]), .in1(out_4[13]), .out(multiplexer_7_out), .sel(not_1_out));
  DFF dff_7 (.clk(clk), .D(multiplexer_7_out), .\output (out_4[13]));
  Multiplexer #(.enable("false")) multiplexer_8 (
    .in0(Input[12]), .in1(out_4[12]), .out(multiplexer_8_out), .sel(not_1_out));
  DFF dff_8 (.clk(clk), .D(multiplexer_8_out), .\output (out_4[12]));
  Multiplexer #(.enable("false")) multiplexer_9 (
    .in0(Input[11]), .in1(out_4[11]), .out(multiplexer_9_out), .sel(not_1_out));
  DFF dff_9 (.clk(clk), .D(multiplexer_9_out), .\output (out_4[11]));
  Multiplexer #(.enable("false")) multiplexer_10 (
    .in0(Input[9]), .in1(out_4[9]), .out(multiplexer_10_out), .sel(not_1_out));
  Multiplexer #(.enable("false")) multiplexer_11 (
    .in0(Input[10]), .in1(out_4[10]), .out(multiplexer_11_out), .sel(not_1_out));
  DFF dff_10 (.clk(clk), .D(multiplexer_11_out), .\output (out_4[10]));
  Multiplexer #(.enable("false")) multiplexer_12 (
    .in0(Input[8]), .in1(out_4[8]), .out(multiplexer_12_out), .sel(not_1_out));
  DFF dff_11 (.clk(clk), .D(multiplexer_12_out), .\output (out_4[8]));
  DFF dff_12 (.clk(clk), .D(multiplexer_10_out), .\output (out_4[9]));
  Multiplexer #(.enable("false")) multiplexer_13 (
    .in0(Input[7]), .in1(out_4[7]), .out(multiplexer_13_out), .sel(not_1_out));
  DFF dff_13 (.clk(clk), .D(multiplexer_13_out), .\output (out_4[7]));
  Multiplexer #(.enable("false")) multiplexer_14 (
    .in0(Input[6]), .in1(out_4[6]), .out(multiplexer_14_out), .sel(not_1_out));
  DFF dff_14 (.clk(clk), .D(multiplexer_14_out), .\output (out_4[6]));
  Multiplexer #(.enable("false")) multiplexer_15 (
    .in0(Input[5]), .in1(out_4[5]), .out(multiplexer_15_out), .sel(not_1_out));
  DFF dff_15 (.clk(clk), .D(multiplexer_15_out), .\output (out_4[5]));
  Multiplexer #(.enable("false")) multiplexer_16 (
    .in0(Input[4]), .in1(out_4[4]), .out(multiplexer_16_out), .sel(not_1_out));
  DFF dff_16 (.clk(clk), .D(multiplexer_16_out), .\output (out_4[4]));
  Multiplexer #(.enable("false")) multiplexer_17 (
    .in0(Input[3]), .in1(out_4[3]), .out(multiplexer_17_out), .sel(not_1_out));
  DFF dff_17 (.clk(clk), .D(multiplexer_17_out), .\output (out_4[3]));
  Multiplexer #(.enable("false")) multiplexer_18 (
    .in0(Input[2]), .in1(out_4[2]), .out(multiplexer_18_out), .sel(not_1_out));
  Multiplexer #(.enable("false")) multiplexer_19 (
    .in0(Input[1]), .in1(out_4[1]), .out(multiplexer_19_out), .sel(not_1_out));
  DFF dff_18 (.clk(clk), .D(multiplexer_18_out), .\output (out_4[2]));
  Multiplexer #(.enable("false")) multiplexer_20 (
    .in0(Input[0]), .in1(out_4[0]), .out(multiplexer_20_out), .sel(not_1_out));
  DFF dff_19 (.clk(clk), .D(multiplexer_20_out), .\output (out_4[0]));
  DFF dff_20 (.clk(clk), .D(multiplexer_19_out), .\output (out_4[1]));
endmodule

module ALU (
  input  [19:0] A,
  input  [19:0] B,
  input  [1:0] select,
  output [19:0] \output 
);

  wire [19:0] and_1_out, n20_bits_adder_1_sum, or_1_out, xor_1_out;

  assign and_1_out = A & B;  // AND_Gate and_1, 20 bits wide
  assign or_1_out = A | B;  // OR_Gate or_1, 20 bits wide
  assign xor_1_out = A ^ B;  // XOR_Gate xor_1, 20 bits wide
  _20_Bits_Adder u_20_bits_adder_1 (.A(A), .B(B), .Sum(n20_bits_adder_1_sum));  // open: cout
  Multiplexer #(.select(2), .width(20), .enable("false")) multiplexer_1 (
    .in0(and_1_out), .in1(or_1_out), .in2(xor_1_out), .in3(n20_bits_adder_1_sum), .out(\output ), .sel(select));
endmodule

module Half_Adder (
  input  A,
  input  B,
  output Sum,
  output Carry
);

  xor xor_1 (Sum, A, B);
  and and_1 (Carry, A, B);
endmodule

module Full_adder (
  input  A,
  input  B,
  input  Carry_In,
  output Sum,
  output Carry_Out
);

  wire and_1_out, and_2_out, xor_1_out;

  xor xor_1 (xor_1_out, A, B);
  xor xor_2 (Sum, xor_1_out, Carry_In);
  and and_1 (and_1_out, Carry_In, xor_1_out);
  and and_2 (and_2_out, B, A);
  or or_1 (Carry_Out, and_1_out, and_2_out);
endmodule

module _4_Bits_Adder (
  input  B3,
  input  B2,
  input  B1,
  input  B0,
  input  A3,
  input  A2,
  input  A1,
  input  A0,
  output Carry_Out,
  output Sum3,
  output Sum2,
  output Sum1,
  output Sum0
);

  wire full_adder_2_carry_out, full_adder_3_carry_out, half_adder_1_carry;

  Full_adder full_adder_1 (.A(A3), .B(B3), .Carry_In(full_adder_2_carry_out), .Sum(Sum3), .Carry_Out(Carry_Out));
  Full_adder full_adder_2 (
    .A(A2), .B(B2), .Carry_In(full_adder_3_carry_out), .Sum(Sum2), .Carry_Out(full_adder_2_carry_out));
  Full_adder full_adder_3 (
    .A(A1), .B(B1), .Carry_In(half_adder_1_carry), .Sum(Sum1), .Carry_Out(full_adder_3_carry_out));
  Half_Adder half_adder_1 (.A(A0), .B(B0), .Sum(Sum0), .Carry(half_adder_1_carry));
endmodule

module _8_Bits_Adder (
  input  B7,
  input  B6,
  input  B5,
  input  B4,
  input  B3,
  input  B2,
  input  B1,
  input  B0,
  input  A7,
  input  A6,
  input  A5,
  input  A4,
  input  A3,
  input  A2,
  input  A1,
  input  A0,
  input  Carry_In,
  output Carry_Out,
  output Sum7,
  output Sum6,
  output Sum5,
  output Sum4,
  output Sum3,
  output Sum2,
  output Sum1,
  output Sum0
);

  wire full_adder_2_carry_out, full_adder_3_carry_out, full_adder_4_carry_out, full_adder_5_carry_out,
       full_adder_6_carry_out, full_adder_7_carry_out, full_adder_8_carry_out;

  Full_adder full_adder_1 (.A(A7), .B(B7), .Carry_In(full_adder_2_carry_out), .Sum(Sum7), .Carry_Out(Carry_Out));
  Full_adder full_adder_2 (
    .A(A6), .B(B6), .Carry_In(full_adder_3_carry_out), .Sum(Sum6), .Carry_Out(full_adder_2_carry_out));
  Full_adder full_adder_3 (
    .A(A5), .B(B5), .Carry_In(full_adder_4_carry_out), .Sum(Sum5), .Carry_Out(full_adder_3_carry_out));
  Full_adder full_adder_4 (
    .A(A4), .B(B4), .Carry_In(full_adder_5_carry_out), .Sum(Sum4), .Carry_Out(full_adder_4_carry_out));
  Full_adder full_adder_5 (
    .A(A3), .B(B3), .Carry_In(full_adder_6_carry_out), .Sum(Sum3), .Carry_Out(full_adder_5_carry_out));
  Full_adder full_adder_6 (
    .A(A2), .B(B2), .Carry_In(full_adder_7_carry_out), .Sum(Sum2), .Carry_Out(full_adder_6_carry_out));
  Full_adder full_adder_7 (
    .A(A1), .B(B1), .Carry_In(full_adder_8_carry_out), .Sum(Sum1), .Carry_Out(full_adder_7_carry_out));
  Full_adder full_adder_8 (.A(A0), .B(B0), .Carry_In(Carry_In), .Sum(Sum0), .Carry_Out(full_adder_8_carry_out));
endmodule

module _20_Bits_Adder (
  input  [19:0] A,
  input  [19:0] B,
  output cout,
  output [19:0] Sum
);

  wire n4_bits_adder_1_carry_out, n8_bits_adder_2_carry_out;

  _8_Bits_Adder u_8_bits_adder_1 (
    .Carry_Out(cout), .B7(B[19]), .A7(A[19]), .B6(B[18]), .A6(A[18]), .B5(B[17]), .A5(A[17]), .B4(B[16]),
    .A4(A[16]), .B3(B[15]), .A3(A[15]), .B2(B[14]), .A2(A[14]), .B1(B[13]), .A1(A[13]), .B0(B[12]),
    .A0(A[12]), .Sum7(Sum[19]), .Sum6(Sum[18]), .Sum5(Sum[17]), .Sum4(Sum[16]), .Sum3(Sum[15]),
    .Sum2(Sum[14]), .Sum1(Sum[13]), .Sum0(Sum[12]), .Carry_In(n8_bits_adder_2_carry_out));
  _4_Bits_Adder u_4_bits_adder_1 (
    .Carry_Out(n4_bits_adder_1_carry_out), .B3(B[3]), .A3(A[3]), .B2(B[2]), .A2(A[2]), .B1(B[1]), .A1(A[1]),
    .B0(B[0]), .A0(A[0]), .Sum3(Sum[3]), .Sum2(Sum[2]), .Sum1(Sum[1]), .Sum0(Sum[0]));
  _8_Bits_Adder u_8_bits_adder_2 (
    .Carry_Out(n8_bits_adder_2_carry_out), .B7(B[11]), .A7(A[11]), .B6(B[10]), .A6(A[10]), .B5(B[9]),
    .A5(A[9]), .B4(B[8]), .A4(A[8]), .B3(B[7]), .A3(A[7]), .B2(B[6]), .A2(A[6]), .B1(B[5]), .A1(A[5]),
    .B0(B[4]), .A0(A[4]), .Sum7(Sum[11]), .Sum6(Sum[10]), .Sum5(Sum[9]), .Sum4(Sum[8]), .Sum3(Sum[7]),
    .Sum2(Sum[6]), .Sum1(Sum[5]), .Sum0(Sum[4]), .Carry_In(n4_bits_adder_1_carry_out));
endmodule

module Processor (
  input  in_1
);

  wire ACS, CCE, DRS, ICS, ISB, ISS, PRS, RWS, WMS;
  wire [1:0] ACD;
  wire [2:0] comparetor_1__3bo, FSMControlType, NZP;
  wire [3:0] REG1, REG2, REG3, registerfileinputdeterminer_1_dr, registerfileinputdeterminer_1_reg1_2,
       registerfileinputdeterminer_1_reg2_2;
  wire [11:0] ADDR;
  wire [19:0] alu_1_output, branchoperator_1_newpc, counter_1_q, IMV, JMP_ADDR, multiplexer_1_out,
       multiplexer_2_out, n20_bits_adder_1_sum, ram_1_data, registerfile_1_output1, registerfile_1_output2,
       registerfileinputdeterminer_1_input_data, rom_1_data;

  _20_Bits_Adder u_20_bits_adder_1 (.A(counter_1_q), .B(JMP_ADDR), .Sum(n20_bits_adder_1_sum));  // open: cout
  Multiplexer #(.width(20), .enable("false")) multiplexer_1 (
    .in0(n20_bits_adder_1_sum), .in1(branchoperator_1_newpc), .out(multiplexer_1_out), .sel(ISB));
  Counter #(.width(20), .max('hfffff)) counter_1 (
    .load(PRS), .D(multiplexer_1_out), .count(CCE), .Q(counter_1_q), .clk(in_1));  // open: carry, clr
  BranchOperator branchoperator_1 (
    .currentPC(counter_1_q), .addr(IMV), .nzp(NZP), .cmpResult(comparetor_1__3bo),
    .newPC(branchoperator_1_newpc));
  ROM #(.addrWidth(20), .dataWidth(20)) rom_1 (.addr(counter_1_q), .data(rom_1_data), .sel(1'b1));
  Comparetor comparetor_1 (
    ._3BO(comparetor_1__3bo), .B(registerfile_1_output2), .A(registerfile_1_output1));  // open: A_B, out_eq, out_gt, out_lt
  ControlUnit controlunit_1 (
    .instruction(rom_1_data), .clk(in_1), .nzp(NZP), ._1reg(REG1), ._2reg(REG2), .ALU_Operation(ACD),
    ._3reg(REG3), .ImmediateControl(ICS), .IMM_Value(IMV), .addr(ADDR), .FSMControlType(FSMControlType),
    .isBranch(ISB), .jump_addr(JMP_ADDR), .pcReadSignal(PRS), .dataMemoryReadSignal(DRS),
    .registerWriteSignal(RWS), .aluControlSignal(ACS), .isStore(ISS), .clockCounterEnabled(CCE),
    .writeMemorySignal(WMS));
  RegisterFile registerfile_1 (
    .inputReg1(registerfileinputdeterminer_1_reg1_2), .input_data(registerfileinputdeterminer_1_input_data),
    .inputReg2(registerfileinputdeterminer_1_reg2_2), .DR(registerfileinputdeterminer_1_dr),
    .WriteEnable(RWS), .clk(in_1), .OUTPUT1(registerfile_1_output1), .OUTPUT2(registerfile_1_output2));
  ALU alu_1 (.A(registerfile_1_output2), .B(multiplexer_2_out), .select(ACD), .\output (alu_1_output));
  Multiplexer #(.width(20), .enable("false")) multiplexer_2 (
    .in0(registerfile_1_output1), .in1(IMV), .out(multiplexer_2_out), .sel(ICS));
  RegisterFileInputDeterminer registerfileinputdeterminer_1 (
    .reg2(REG2), .reg1(REG1), .input_data(registerfileinputdeterminer_1_input_data), .reg3(REG3),
    .isArithmetic(ACS), .isBranch(ISB), .reg2_2(registerfileinputdeterminer_1_reg2_2), .RAM(ram_1_data),
    .dr(registerfileinputdeterminer_1_dr), .reg1_2(registerfileinputdeterminer_1_reg1_2), .ALU(alu_1_output),
    .isStore(ISS));
  RAM #(.addrWidth(12), .dataWidth(20), .bus("separate")) ram_1 (
    .addr(ADDR), .din(registerfile_1_output1), .data(ram_1_data), .str(WMS), .clk(in_1), .ld(DRS));  // open: sel, clr

  // Notes on the sheet:
  //   contents of rom_1 (hex, n*v repeats v):
  //   d1000 d2001 3120 73003
endmodule

// CMP
module Comparetor (
  input  [19:0] B,
  input  [19:0] A,
  output out_eq,
  output out_gt,
  output [19:0] A_B,
  output out_lt,
  output [2:0] _3BO
);

  wire not_2_out, not_3_out;
  wire [19:0] n20_bits_adder_1_sum, not_1_out;

  assign not_1_out = ~B;  // NOT_Gate not_1, 20 bits wide
  _20_Bits_Adder u_20_bits_adder_1 (.A(not_1_out), .B(20'h1), .Sum(n20_bits_adder_1_sum));  // open: cout
  _20_Bits_Adder u_20_bits_adder_2 (.A(A), .B(n20_bits_adder_1_sum), .Sum({_3BO[2], A_B[18:0]}));  // open: cout
  nor nor_1 (_3BO[1], A_B[0], A_B[1], A_B[2], A_B[3], A_B[4], A_B[5], A_B[6], A_B[7], A_B[8], A_B[9], A_B[10], A_B[11], A_B[12], A_B[13], A_B[14], A_B[15], A_B[16], A_B[17], A_B[18], _3BO[2]);
  not not_2 (not_2_out, _3BO[2]);
  not not_3 (not_3_out, _3BO[1]);
  and and_1 (_3BO[0], not_3_out, not_2_out);

  assign A_B[19] = _3BO[2];
  assign out_eq = _3BO[1];
  assign out_gt = _3BO[0];
  assign out_lt = _3BO[2];
endmodule

// REGFILE
module RegisterFile (
  input  [3:0] inputReg1,
  input  [19:0] input_data,
  input  [3:0] inputReg2,
  input  [3:0] DR,
  input  WriteEnable,
  input  clk,
  output [19:0] OUTPUT1,
  output [19:0] OUTPUT2
);

  wire and_1_out, and_2_out, and_3_out, and_4_out, and_5_out, and_6_out, and_7_out, and_8_out, and_9_out,
       and_10_out, and_11_out, and_12_out, and_13_out, and_14_out, and_15_out, and_16_out, decoder_1_out0,
       decoder_1_out1, decoder_1_out2, decoder_1_out3, decoder_1_out4, decoder_1_out5, decoder_1_out6,
       decoder_1_out7, decoder_1_out8, decoder_1_out9, decoder_1_out10, decoder_1_out11, decoder_1_out12,
       decoder_1_out13, decoder_1_out14, decoder_1_out15;
  wire [19:0] register_1_q, register_2_q, register_3_q, register_4_q, register_5_q, register_6_q,
       register_7_q, register_8_q, register_9_q, register_10_q, register_11_q, register_12_q, register_13_q,
       register_14_q, register_15_q, register_16_q;

  Decoder #(.select(4), .enable("false")) decoder_1 (
    .out0(decoder_1_out0), .out1(decoder_1_out1), .out2(decoder_1_out2), .out3(decoder_1_out3),
    .out4(decoder_1_out4), .out5(decoder_1_out5), .out6(decoder_1_out6), .out7(decoder_1_out7),
    .out8(decoder_1_out8), .out9(decoder_1_out9), .out10(decoder_1_out10), .out11(decoder_1_out11),
    .out12(decoder_1_out12), .out13(decoder_1_out13), .out14(decoder_1_out14), .out15(decoder_1_out15),
    .sel(DR));
  and and_1 (and_1_out, decoder_1_out0, WriteEnable);
  and and_2 (and_2_out, decoder_1_out1, WriteEnable);
  and and_3 (and_3_out, decoder_1_out2, WriteEnable);
  and and_4 (and_4_out, decoder_1_out3, WriteEnable);
  and and_5 (and_5_out, decoder_1_out4, WriteEnable);
  and and_6 (and_6_out, decoder_1_out5, WriteEnable);
  and and_7 (and_7_out, decoder_1_out6, WriteEnable);
  and and_8 (and_8_out, decoder_1_out7, WriteEnable);
  and and_9 (and_9_out, decoder_1_out8, WriteEnable);
  and and_10 (and_10_out, decoder_1_out9, WriteEnable);
  and and_11 (and_11_out, decoder_1_out10, WriteEnable);
  and and_12 (and_12_out, decoder_1_out11, WriteEnable);
  and and_13 (and_13_out, decoder_1_out12, WriteEnable);
  and and_14 (and_14_out, decoder_1_out13, WriteEnable);
  and and_15 (and_15_out, decoder_1_out14, WriteEnable);
  and and_16 (and_16_out, decoder_1_out15, WriteEnable);
  Register_part #(.width(20)) register_1 (.D(input_data), .en(and_1_out), .Q(register_1_q), .clk(clk));  // open: clr
  Register_part #(.width(20)) register_2 (.D(input_data), .en(and_2_out), .Q(register_2_q), .clk(clk));  // open: clr
  Register_part #(.width(20)) register_3 (.D(input_data), .en(and_3_out), .Q(register_3_q), .clk(clk));  // open: clr
  Register_part #(.width(20)) register_4 (.D(input_data), .en(and_4_out), .Q(register_4_q), .clk(clk));  // open: clr
  Register_part #(.width(20)) register_5 (.D(input_data), .en(and_5_out), .Q(register_5_q), .clk(clk));  // open: clr
  Register_part #(.width(20)) register_6 (.D(input_data), .en(and_6_out), .Q(register_6_q), .clk(clk));  // open: clr
  Register_part #(.width(20)) register_7 (.D(input_data), .en(and_7_out), .Q(register_7_q), .clk(clk));  // open: clr
  Register_part #(.width(20)) register_8 (.D(input_data), .en(and_8_out), .Q(register_8_q), .clk(clk));  // open: clr
  Register_part #(.width(20)) register_9 (.D(input_data), .en(and_9_out), .Q(register_9_q), .clk(clk));  // open: clr
  Register_part #(.width(20)) register_10 (.D(input_data), .en(and_10_out), .Q(register_10_q), .clk(clk));  // open: clr
  Register_part #(.width(20)) register_11 (.D(input_data), .en(and_11_out), .Q(register_11_q), .clk(clk));  // open: clr
  Register_part #(.width(20)) register_12 (.D(input_data), .en(and_12_out), .Q(register_12_q), .clk(clk));  // open: clr
  Register_part #(.width(20)) register_13 (.D(input_data), .en(and_13_out), .Q(register_13_q), .clk(clk));  // open: clr
  Register_part #(.width(20)) register_14 (.D(input_data), .en(and_14_out), .Q(register_14_q), .clk(clk));  // open: clr
  Register_part #(.width(20)) register_15 (.D(input_data), .en(and_15_out), .Q(register_15_q), .clk(clk));  // open: clr
  Register_part #(.width(20)) register_16 (.D(input_data), .en(and_16_out), .Q(register_16_q), .clk(clk));  // open: clr
  Multiplexer #(.select(4), .width(20), .enable("false")) multiplexer_1 (
    .in0(register_1_q), .in1(register_2_q), .in2(register_3_q), .in3(register_4_q), .in4(register_5_q),
    .in5(register_6_q), .in6(register_7_q), .in7(register_8_q), .in8(register_9_q), .in9(register_10_q),
    .in10(register_11_q), .in11(register_12_q), .in12(register_13_q), .in13(register_14_q),
    .in14(register_15_q), .in15(register_16_q), .out(OUTPUT1), .sel(inputReg1));
  Multiplexer #(.select(4), .width(20), .enable("false")) multiplexer_2 (
    .in0(register_1_q), .in1(register_2_q), .in2(register_3_q), .in3(register_4_q), .in4(register_5_q),
    .in5(register_6_q), .in6(register_7_q), .in7(register_8_q), .in8(register_9_q), .in9(register_10_q),
    .in10(register_11_q), .in11(register_12_q), .in12(register_13_q), .in13(register_14_q),
    .in14(register_15_q), .in15(register_16_q), .out(OUTPUT2), .sel(inputReg2));
endmodule

module BitExtender (
  input  inpu,
  output [19:0] outpu
);


  assign outpu = {20{inpu}};
endmodule

// Control Unit
module ControlUnit (
  input  [19:0] instruction,
  input  clk,
  output [2:0] nzp,
  output [3:0] _1reg,
  output [3:0] _2reg,
  output [1:0] ALU_Operation,
  output [3:0] _3reg,
  output ImmediateControl,
  output [19:0] IMM_Value,
  output [11:0] addr,
  output [2:0] FSMControlType,
  output isBranch,
  output [19:0] jump_addr,
  output pcReadSignal,
  output dataMemoryReadSignal,
  output registerWriteSignal,
  output aluControlSignal,
  output isStore,
  output clockCounterEnabled,
  output writeMemorySignal
);

  wire ADD, ADDI, ALU_CONTROL, AND, ANDI, BEQ, BGE, BGT, BLE, BLT, JUMP, LD, OR, or_1_out, or_2_out,
       or_3_out, or_4_out, ORI, ST, XOR, XORI;
  wire [6:0] register_1_q;

  Decoder #(.select(4), .enable("false")) decoder_1 (
    .out0(ADD), .out1(ADDI), .out2(BGT), .out3(JUMP), .out4(BEQ), .out5(XOR), .out6(BGE), .out7(ST),
    .out8(BLT), .out9(XORI), .out10(AND), .out11(ANDI), .out12(BLE), .out13(LD), .out14(OR), .out15(ORI),
    .sel(instruction[19:16]));
  or or_1 (or_1_out, AND, ANDI);
  or or_2 (or_2_out, OR, ORI);
  or or_3 (or_3_out, XOR, XORI);
  or or_4 (or_4_out, ADD, ADDI);
  Priority_Encoder #(.select(2)) priority_encoder_1 (
    .in0(or_1_out), .in1(or_2_out), .in2(or_3_out), .in3(or_4_out), .out(ALU_Operation));  // open: gs, en_out, en_in
  or or_5 (isBranch, BEQ, BGT, BGE, BLE, BLT);
  or or_6 (ALU_CONTROL, or_4_out, or_3_out, or_2_out, or_1_out);
  or or_7 (ImmediateControl, ANDI, ORI, XORI, ADDI);
  FiniteStateMachine finitestatemachine_1 (
    .pcReadSignal(register_1_q[0]), .dataMemoryReadSignal(register_1_q[1]),
    .registerWriteSignal(register_1_q[2]), .aluControlSignal(register_1_q[3]), .isStore(register_1_q[4]),
    .clockCounterEnabled(register_1_q[5]), .writeMemorySignal(register_1_q[6]), .id0(FSMControlType[2]),
    .id1(FSMControlType[1]), .id2(FSMControlType[0]), .pcReadSignal_2(pcReadSignal),
    .memoryRead(dataMemoryReadSignal), .registerWriteSignal_2(registerWriteSignal),
    .aluControlSignal_2(aluControlSignal), .isStore_2(isStore), .clockCounterEnabled_2(clockCounterEnabled),
    .writeMemorySignal_2(writeMemorySignal));
  Register_part #(.width(7)) register_1 (
    .D({writeMemorySignal, clockCounterEnabled, isStore, aluControlSignal, registerWriteSignal, dataMemoryReadSignal, pcReadSignal}),
    .en(1'b1), .Q(register_1_q), .clk(clk));  // open: clr
  Priority_Encoder priority_encoder_2 (
    .in0(ALU_CONTROL), .in1(JUMP), .in2(LD), .in3(isBranch), .in4(ST), .out(FSMControlType));  // open: in5, in6, in7, en_in, gs, en_out

  assign _1reg = instruction[15:12];
  assign _2reg = instruction[11:8];
  assign _3reg = instruction[7:4];
  assign addr = instruction[11:0];
  assign IMM_Value = {{13{instruction[7]}}, instruction[6:0]};
  assign jump_addr = {{5{instruction[15]}}, instruction[14:0]};
  assign nzp = instruction[19:17];

  // Other names for the same wires on the sheet: BRANCH_CONTROL = isBranch; FSM_BIT[2:0] = FSMControlType;
  //   IMM[19:0] = {{13{instruction[7]}}, instruction[6:0]};
  //   JMP_ADDR[19:0] = {{5{instruction[15]}}, instruction[14:0]}; JUMP_CONTROL = JUMP; LD_CONTROL = LD;
  //   OPCODE[3:0] = instruction[19:16]; ST_CONTROL = ST

  // Notes on the sheet:
  //   ALU Operants
  //   1st Reg
  //   2nd Reg
  //   3rd Reg
endmodule

// finite state
module FiniteStateMachine (
  input  pcReadSignal,
  input  dataMemoryReadSignal,
  input  registerWriteSignal,
  input  aluControlSignal,
  input  isStore,
  input  clockCounterEnabled,
  input  writeMemorySignal,
  input  id0,
  input  id1,
  input  id2,
  output pcReadSignal_2,
  output memoryRead,
  output registerWriteSignal_2,
  output aluControlSignal_2,
  output isStore_2,
  output clockCounterEnabled_2,
  output writeMemorySignal_2
);

  wire and_1_out, and_2_out, and_3_out, and_4_out, and_5_out, and_11_out, and_12_out, not_1_out, not_2_out,
       not_3_out, not_4_out, not_5_out, not_6_out, not_7_out, not_8_out, not_9_out, not_10_out, not_11_out,
       not_12_out, not_13_out, not_14_out, not_15_out, not_16_out, not_17_out, not_18_out, not_19_out,
       not_20_out, not_21_out, not_23_out, not_24_out, not_26_out, not_27_out, not_28_out, not_30_out,
       not_31_out, or_1_out, or_2_out, r1, r2;

  not not_1 (not_1_out, pcReadSignal);
  not not_2 (not_2_out, clockCounterEnabled);
  not not_3 (not_3_out, clockCounterEnabled);
  not not_4 (not_4_out, pcReadSignal);
  not not_5 (not_5_out, id0);
  not not_6 (not_6_out, id0);
  not not_7 (not_7_out, id2);
  not not_8 (not_8_out, id0);
  not not_9 (not_9_out, id2);
  not not_10 (not_10_out, id0);
  not not_11 (not_11_out, id1);
  not not_12 (not_12_out, id2);
  not not_13 (not_13_out, id1);
  not not_14 (not_14_out, id2);
  not not_15 (not_15_out, aluControlSignal);
  and and_1 (and_1_out, dataMemoryReadSignal, not_15_out, id1);
  not not_16 (not_16_out, dataMemoryReadSignal);
  and and_2 (and_2_out, not_16_out, aluControlSignal, not_17_out);
  not not_17 (not_17_out, id1);
  not not_18 (not_18_out, pcReadSignal);
  not not_19 (not_19_out, dataMemoryReadSignal);
  not not_20 (not_20_out, registerWriteSignal);
  not not_21 (not_21_out, aluControlSignal);
  // NOT_Gate not_22 has open pins: in=clockCounterEnabled, out=open
  not not_23 (not_23_out, id1);
  not not_24 (not_24_out, id2);
  and and_3 (and_3_out, not_1_out, not_2_out);
  and and_4 (and_4_out, pcReadSignal, not_3_out);
  and and_5 (and_5_out, not_4_out, clockCounterEnabled);
  not not_25 (r2, or_1_out);
  or or_1 (or_1_out, dataMemoryReadSignal, registerWriteSignal, aluControlSignal, isStore, writeMemorySignal);
  and and_6 (pcReadSignal_2, r2, not_5_out, id1, id2, r1);
  and and_7 (memoryRead, r2, not_6_out, id1, not_7_out, r1);
  and and_8 (registerWriteSignal_2, r2, not_8_out, not_9_out, r1);
  and and_9 (aluControlSignal_2, r2, not_10_out, not_11_out, not_12_out, r1);
  and and_10 (isStore_2, r2, id0, not_13_out, not_14_out, r1);
  or or_2 (or_2_out, and_1_out, and_2_out);
  and and_11 (and_11_out, not_18_out, not_19_out, not_20_out, not_21_out, isStore, writeMemorySignal, id0, not_23_out, not_24_out);
  or or_3 (r1, and_3_out, and_4_out, and_5_out);
  not not_26 (not_26_out, pcReadSignal);
  not not_27 (not_27_out, isStore);
  not not_28 (not_28_out, clockCounterEnabled);
  // NOT_Gate not_29 has open pins: in=writeMemorySignal, out=open
  and and_12 (and_12_out, not_26_out, registerWriteSignal, not_27_out, not_28_out, not_30_out, not_31_out, or_2_out);
  not not_30 (not_30_out, id0);
  not not_31 (not_31_out, id2);
  or or_4 (clockCounterEnabled_2, and_12_out, and_11_out);

  assign writeMemorySignal_2 = isStore_2;
endmodule

// DTRM
module RegisterFileInputDeterminer (
  input  [3:0] reg3,
  input  [3:0] reg2,
  input  [19:0] RAM,
  input  [3:0] reg1,
  input  [19:0] ALU,
  input  isArithmetic,
  input  isBranch,
  input  isStore,
  output [3:0] reg2_2,
  output [3:0] dr,
  output [19:0] input_data,
  output [3:0] reg1_2
);

  wire [3:0] demultiplexer_1_out0, demultiplexer_1_out1, demultiplexer_2_out1, multiplexer_2_out;

  Demultiplexer #(.width(4), .enable("false")) demultiplexer_1 (
    .out0(demultiplexer_1_out0), .out1(demultiplexer_1_out1), .in(reg2), .sel(isBranch));
  Demultiplexer #(.width(4), .enable("false")) demultiplexer_2 (
    .out0(dr), .out1(demultiplexer_2_out1), .in(reg1), .sel(isBranch));
  Multiplexer #(.width(4), .enable("false")) multiplexer_1 (
    .in0(reg3), .in1(demultiplexer_1_out1), .out(reg2_2), .sel(isBranch));
  Multiplexer #(.width(4), .enable("false")) multiplexer_2 (
    .in0(demultiplexer_1_out0), .in1(demultiplexer_2_out1), .out(multiplexer_2_out), .sel(isBranch));
  Multiplexer #(.width(4), .enable("false")) multiplexer_3 (
    .in0(multiplexer_2_out), .in1(reg1), .out(reg1_2), .sel(isStore));
  Multiplexer #(.width(20), .enable("false")) multiplexer_4 (
    .in0(RAM), .in1(ALU), .out(input_data), .sel(isArithmetic));
endmodule

// BRO
module BranchOperator (
  input  [19:0] currentPC,
  input  [19:0] addr,
  input  [2:0] nzp,
  input  [2:0] cmpResult,
  output [19:0] newPC
);

  wire [2:0] and_1_out;
  wire [19:0] n20_bits_adder_1_sum, n20_bits_adder_2_sum;

  assign and_1_out = nzp & cmpResult;  // AND_Gate and_1, 3 bits wide
  _20_Bits_Adder u_20_bits_adder_1 (.A(20'h1), .B(currentPC), .Sum(n20_bits_adder_1_sum));  // open: cout
  _20_Bits_Adder u_20_bits_adder_2 (.A(currentPC), .B(addr), .Sum(n20_bits_adder_2_sum));  // open: cout
  Multiplexer #(.select(3), .width(20), .enable("false")) multiplexer_1 (
    .in0(n20_bits_adder_1_sum), .in1(n20_bits_adder_2_sum), .in2(n20_bits_adder_2_sum),
    .in3(n20_bits_adder_2_sum), .in4(n20_bits_adder_2_sum), .in5(n20_bits_adder_2_sum),
    .in6(n20_bits_adder_2_sum), .in7(n20_bits_adder_2_sum), .out(newPC), .sel(and_1_out));
endmodule
