// Logisim project FROG.circ as structural Verilog: 12 circuits, main circuit main
module main (
  input  clk
);

  wire controlunit_1_imm, controlunit_1_irld, controlunit_1_ld, controlunit_1_mux, controlunit_1_pc_plus_plus;
  wire [1:0] ir_1_dataout, ir_1_dataout_3, ir_1_dataout_4;
  wire [3:0] ir_1_dataout_5;
  wire [5:2] ir_1_dataout_2;
  wire [15:0] alu_1_result, multiplexer_1_out, multiplexer_2_out, multiplexer_3_out, multiplexer_4_out,
       n16bitregwithinc_1_out, regbank_1_dout0, regbank_1_dout1, regbank_1_dout2, regbank_1_dout3, rom_1_data;

  _16bitRegWithInc u_16bitregwithinc_1 (
    .datain({16{1'b0}}), .out(n16bitregwithinc_1_out), .incr(controlunit_1_pc_plus_plus), .load(1'b0),
    .clk(clk));
  ROM #(.addrWidth(16), .dataWidth(16)) rom_1 (.addr(n16bitregwithinc_1_out), .data(rom_1_data));  // open: sel
  regbank regbank_1 (
    .Reg_Select(ir_1_dataout), .Reg_Load(controlunit_1_ld), .DATAIN(multiplexer_1_out),
    .DOUT0(regbank_1_dout0), .DOUT1(regbank_1_dout1), .DOUT2(regbank_1_dout2), .DOUT3(regbank_1_dout3),
    .CLK(clk));
  Multiplexer #(.width(16)) multiplexer_1 (
    .in0(alu_1_result), .in1(rom_1_data), .out(multiplexer_1_out), .sel(controlunit_1_mux));  // open: en
  Multiplexer #(.select(2), .width(16)) multiplexer_2 (
    .in0(regbank_1_dout0), .in1(regbank_1_dout1), .in2(regbank_1_dout2), .in3(regbank_1_dout3),
    .out(multiplexer_2_out), .sel(ir_1_dataout_4));  // open: en
  Hex_Digit_Display hex_digit_display_1 (.value(regbank_1_dout0[11:8]));  // open: dp
  Hex_Digit_Display hex_digit_display_2 (.value(regbank_1_dout0[15:12]));  // open: dp
  Multiplexer #(.select(2), .width(16)) multiplexer_3 (
    .in0(regbank_1_dout0), .in1(regbank_1_dout1), .in2(regbank_1_dout2), .in3(regbank_1_dout3),
    .out(multiplexer_3_out), .sel(ir_1_dataout_3));  // open: en
  Multiplexer #(.width(16)) multiplexer_4 (
    .in0(multiplexer_3_out), .in1(rom_1_data), .out(multiplexer_4_out), .sel(controlunit_1_imm));  // open: en
  ALU alu_1 (.alu_select(ir_1_dataout_5), .Din1(multiplexer_2_out), .Din2(multiplexer_4_out), .RESULT(alu_1_result));
  Hex_Digit_Display hex_digit_display_3 (.value(regbank_1_dout0[7:4]));  // open: dp
  Hex_Digit_Display hex_digit_display_4 (.value(regbank_1_dout0[3:0]));  // open: dp
  IR ir_1 (
    .DATAIN(rom_1_data[11:0]),
    .DATAOUT({ir_1_dataout_5, ir_1_dataout_4, ir_1_dataout_2[5], ir_1_dataout_3, ir_1_dataout_2[2], ir_1_dataout}),
    .LOAD(controlunit_1_irld), .CLK(clk));
  ControlUnit controlunit_1 (
    .clk(clk), .PC_plus_plus(controlunit_1_pc_plus_plus), .IRLD(controlunit_1_irld), .MUX(controlunit_1_mux),
    .LD(controlunit_1_ld), .in(rom_1_data[15:14]), .imm(controlunit_1_imm));

  // Notes on the sheet:
  //   contents of rom_1 (hex, n*v repeats v):
  //   0 4000 9 4001 5 4002 0 800b 0 80da a
endmodule

// REG
module _16bitReg (
  input  [15:0] DATAIN,
  input  LOAD,
  input  CLK,
  output [15:0] DATAOUT
);

  wire and_1_out, and_2_out, and_3_out, and_4_out, and_5_out, and_6_out, and_7_out, and_8_out, and_9_out,
       and_10_out, and_11_out, and_12_out, and_13_out, and_14_out, and_15_out, and_16_out, and_17_out,
       and_18_out, and_19_out, and_20_out, and_21_out, and_22_out, and_23_out, and_24_out, and_25_out,
       and_26_out, and_27_out, and_28_out, and_29_out, and_30_out, and_31_out, and_32_out, not_1_out,
       not_2_out, not_3_out, not_4_out, not_5_out, not_6_out, not_7_out, not_8_out, not_9_out, not_10_out,
       not_11_out, not_12_out, not_13_out, not_14_out, not_15_out, not_16_out, s_r_ff_1_qn, s_r_ff_2_qn,
       s_r_ff_3_qn, s_r_ff_4_qn, s_r_ff_5_qn, s_r_ff_6_qn, s_r_ff_7_qn, s_r_ff_8_qn, s_r_ff_9_qn,
       s_r_ff_10_qn, s_r_ff_11_qn, s_r_ff_12_qn, s_r_ff_13_qn, s_r_ff_14_qn, s_r_ff_15_qn, s_r_ff_16_qn;

  not not_1 (not_1_out, DATAIN[0]);
  not not_2 (not_2_out, DATAIN[1]);
  not not_3 (not_3_out, DATAIN[2]);
  not not_4 (not_4_out, DATAIN[3]);
  not not_5 (not_5_out, DATAIN[4]);
  not not_6 (not_6_out, DATAIN[5]);
  not not_7 (not_7_out, DATAIN[6]);
  not not_8 (not_8_out, DATAIN[7]);
  not not_9 (not_9_out, DATAIN[8]);
  not not_10 (not_10_out, DATAIN[9]);
  not not_11 (not_11_out, DATAIN[10]);
  not not_12 (not_12_out, DATAIN[11]);
  not not_13 (not_13_out, DATAIN[12]);
  not not_14 (not_14_out, DATAIN[13]);
  not not_15 (not_15_out, DATAIN[14]);
  not not_16 (not_16_out, DATAIN[15]);
  and and_1 (and_1_out, DATAIN[0], LOAD);
  and and_2 (and_2_out, not_1_out, LOAD);
  and and_3 (and_3_out, DATAIN[1], LOAD);
  and and_4 (and_4_out, not_2_out, LOAD);
  and and_5 (and_5_out, DATAIN[2], LOAD);
  and and_6 (and_6_out, not_3_out, LOAD);
  and and_7 (and_7_out, DATAIN[3], LOAD);
  and and_8 (and_8_out, not_4_out, LOAD);
  and and_9 (and_9_out, DATAIN[4], LOAD);
  and and_10 (and_10_out, not_5_out, LOAD);
  and and_11 (and_11_out, DATAIN[5], LOAD);
  and and_12 (and_12_out, not_6_out, LOAD);
  and and_13 (and_13_out, DATAIN[6], LOAD);
  and and_14 (and_14_out, not_7_out, LOAD);
  and and_15 (and_15_out, DATAIN[7], LOAD);
  and and_16 (and_16_out, not_8_out, LOAD);
  and and_17 (and_17_out, DATAIN[8], LOAD);
  and and_18 (and_18_out, not_9_out, LOAD);
  and and_19 (and_19_out, DATAIN[9], LOAD);
  and and_20 (and_20_out, not_10_out, LOAD);
  and and_21 (and_21_out, DATAIN[10], LOAD);
  and and_22 (and_22_out, not_11_out, LOAD);
  and and_23 (and_23_out, DATAIN[11], LOAD);
  and and_24 (and_24_out, not_12_out, LOAD);
  and and_25 (and_25_out, DATAIN[12], LOAD);
  and and_26 (and_26_out, not_13_out, LOAD);
  and and_27 (and_27_out, DATAIN[13], LOAD);
  and and_28 (and_28_out, not_14_out, LOAD);
  and and_29 (and_29_out, DATAIN[14], LOAD);
  and and_30 (and_30_out, not_15_out, LOAD);
  and and_31 (and_31_out, DATAIN[15], LOAD);
  and and_32 (and_32_out, not_16_out, LOAD);
  S_R_Flip_Flop s_r_ff_1 (
    .S(and_1_out), .clk(CLK), .R(and_2_out), .Q(DATAOUT[0]), .Qn(s_r_ff_1_qn));  // open: preset, reset, en
  S_R_Flip_Flop s_r_ff_2 (
    .S(and_3_out), .clk(CLK), .R(and_4_out), .Q(DATAOUT[1]), .Qn(s_r_ff_2_qn));  // open: preset, reset, en
  S_R_Flip_Flop s_r_ff_3 (
    .S(and_5_out), .clk(CLK), .R(and_6_out), .Q(DATAOUT[2]), .Qn(s_r_ff_3_qn));  // open: preset, reset, en
  S_R_Flip_Flop s_r_ff_4 (
    .S(and_7_out), .clk(CLK), .R(and_8_out), .Q(DATAOUT[3]), .Qn(s_r_ff_4_qn));  // open: preset, reset, en
  S_R_Flip_Flop s_r_ff_5 (
    .S(and_9_out), .clk(CLK), .R(and_10_out), .Q(DATAOUT[4]), .Qn(s_r_ff_5_qn));  // open: preset, reset, en
  S_R_Flip_Flop s_r_ff_6 (
    .S(and_11_out), .clk(CLK), .R(and_12_out), .Q(DATAOUT[5]), .Qn(s_r_ff_6_qn));  // open: preset, reset, en
  S_R_Flip_Flop s_r_ff_7 (
    .S(and_13_out), .clk(CLK), .R(and_14_out), .Q(DATAOUT[6]), .Qn(s_r_ff_7_qn));  // open: preset, reset, en
  S_R_Flip_Flop s_r_ff_8 (
    .S(and_15_out), .clk(CLK), .R(and_16_out), .Q(DATAOUT[7]), .Qn(s_r_ff_8_qn));  // open: preset, reset, en
  S_R_Flip_Flop s_r_ff_9 (
    .S(and_17_out), .clk(CLK), .R(and_18_out), .Q(DATAOUT[8]), .Qn(s_r_ff_9_qn));  // open: preset, reset, en
  S_R_Flip_Flop s_r_ff_10 (
    .S(and_19_out), .clk(CLK), .R(and_20_out), .Q(DATAOUT[9]), .Qn(s_r_ff_10_qn));  // open: preset, reset, en
  S_R_Flip_Flop s_r_ff_11 (
    .S(and_21_out), .clk(CLK), .R(and_22_out), .Q(DATAOUT[10]), .Qn(s_r_ff_11_qn));  // open: preset, reset, en
  S_R_Flip_Flop s_r_ff_12 (
    .S(and_23_out), .clk(CLK), .R(and_24_out), .Q(DATAOUT[11]), .Qn(s_r_ff_12_qn));  // open: preset, reset, en
  S_R_Flip_Flop s_r_ff_13 (
    .S(and_25_out), .clk(CLK), .R(and_26_out), .Q(DATAOUT[12]), .Qn(s_r_ff_13_qn));  // open: preset, reset, en
  S_R_Flip_Flop s_r_ff_14 (
    .S(and_27_out), .clk(CLK), .R(and_28_out), .Q(DATAOUT[13]), .Qn(s_r_ff_14_qn));  // open: preset, reset, en
  S_R_Flip_Flop s_r_ff_15 (
    .S(and_29_out), .clk(CLK), .R(and_30_out), .Q(DATAOUT[14]), .Qn(s_r_ff_15_qn));  // open: preset, reset, en
  S_R_Flip_Flop s_r_ff_16 (
    .S(and_31_out), .clk(CLK), .R(and_32_out), .Q(DATAOUT[15]), .Qn(s_r_ff_16_qn));  // open: preset, reset, en
endmodule

// REGBANK
module regbank (
  input  [1:0] Reg_Select,
  input  Reg_Load,
  input  [15:0] DATAIN,
  input  CLK,
  output [15:0] DOUT0,
  output [15:0] DOUT1,
  output [15:0] DOUT2,
  output [15:0] DOUT3
);

  wire and_1_out, and_2_out, and_3_out, and_4_out, decoder_1_out0, decoder_1_out1, decoder_1_out2,
       decoder_1_out3;

  Decoder #(.select(2)) decoder_1 (
    .out0(decoder_1_out0), .out1(decoder_1_out1), .out2(decoder_1_out2), .out3(decoder_1_out3),
    .sel(Reg_Select));  // open: en
  and and_1 (and_1_out, decoder_1_out0, Reg_Load);
  and and_2 (and_2_out, decoder_1_out1, Reg_Load);
  and and_3 (and_3_out, decoder_1_out2, Reg_Load);
  and and_4 (and_4_out, decoder_1_out3, Reg_Load);
  _16bitReg REG0 (.DATAIN(DATAIN), .LOAD(and_1_out), .CLK(CLK), .DATAOUT(DOUT0));
  _16bitReg REG1 (.DATAIN(DATAIN), .LOAD(and_2_out), .CLK(CLK), .DATAOUT(DOUT1));
  _16bitReg REG2 (.DATAIN(DATAIN), .LOAD(and_3_out), .CLK(CLK), .DATAOUT(DOUT2));
  _16bitReg REG3 (.DATAIN(DATAIN), .LOAD(and_4_out), .CLK(CLK), .DATAOUT(DOUT3));
endmodule

module ALU (
  input  [15:0] Din1,
  input  [15:0] Din2,
  input  [3:0] alu_select,
  output [15:0] RESULT
);

  wire [15:0] adder_1_out, adder_2_out, bitwise_and_1_out, bitwise_or_1_out, bitwise_xor_1_out, not_1_out,
       subtractor_1_out, subtractor_2_out;

  Adder #(.width(16)) adder_1 (.a(Din1), .b(Din2), .out(adder_1_out));  // open: cin, cout
  Subtractor #(.width(16)) subtractor_1 (.a(Din1), .b(Din2), .out(subtractor_1_out));  // open: bin, bout
  bitwise_and bitwise_and_1 (.in1(Din1), .in2(Din2), .out(bitwise_and_1_out));
  bitwise_or bitwise_or_1 (.in1(Din1), .in2(Din2), .out(bitwise_or_1_out));
  bitwise_xor bitwise_xor_1 (.in1(Din1), .in2(Din2), .out(bitwise_xor_1_out));
  assign not_1_out = ~Din1;  // NOT_Gate not_1, 16 bits wide
  Adder #(.width(16)) adder_2 (.a(Din1), .b(16'h1), .out(adder_2_out));  // open: cin, cout
  Subtractor #(.width(16)) subtractor_2 (.a(Din1), .b(16'h1), .out(subtractor_2_out));  // open: bin, bout
  Multiplexer #(.select(4), .width(16)) multiplexer_1 (
    .in0(adder_1_out), .in1(subtractor_1_out), .in2(bitwise_and_1_out), .in3(bitwise_or_1_out),
    .in4(bitwise_xor_1_out), .in5(not_1_out), .in6(Din1), .in7(adder_2_out), .in8(subtractor_2_out),
    .out(RESULT), .sel(alu_select));  // open: in9, in10, in11, in12, in13, in14, in15, en
endmodule

// AND
module bitwise_and (
  input  [15:0] in1,
  input  [15:0] in2,
  output [15:0] out
);

  and and_1 (out[0], in2[0], in1[0]);
  and and_2 (out[1], in2[1], in1[1]);
  and and_3 (out[2], in2[2], in1[2]);
  and and_4 (out[3], in2[3], in1[3]);
  and and_5 (out[4], in2[4], in1[4]);
  and and_6 (out[5], in2[5], in1[5]);
  and and_7 (out[6], in2[6], in1[6]);
  and and_8 (out[7], in2[7], in1[7]);
  and and_9 (out[8], in2[8], in1[8]);
  and and_10 (out[9], in2[9], in1[9]);
  and and_11 (out[10], in2[10], in1[10]);
  and and_12 (out[11], in2[11], in1[11]);
  and and_13 (out[12], in2[12], in1[12]);
  and and_14 (out[13], in2[13], in1[13]);
  and and_15 (out[14], in2[14], in1[14]);
  and and_16 (out[15], in2[15], in1[15]);
endmodule

// OR
module bitwise_or (
  input  [15:0] in1,
  input  [15:0] in2,
  output [15:0] out
);

  or or_1 (out[0], in2[0], in1[0]);
  or or_2 (out[1], in2[1], in1[1]);
  or or_3 (out[2], in2[2], in1[2]);
  or or_4 (out[3], in2[3], in1[3]);
  or or_5 (out[4], in2[4], in1[4]);
  or or_6 (out[5], in2[5], in1[5]);
  or or_7 (out[6], in2[6], in1[6]);
  or or_8 (out[7], in2[7], in1[7]);
  or or_9 (out[8], in2[8], in1[8]);
  or or_10 (out[9], in2[9], in1[9]);
  or or_11 (out[10], in2[10], in1[10]);
  or or_12 (out[11], in2[11], in1[11]);
  or or_13 (out[12], in2[12], in1[12]);
  or or_14 (out[13], in2[13], in1[13]);
  or or_15 (out[14], in2[14], in1[14]);
  or or_16 (out[15], in2[15], in1[15]);
endmodule

// XOR
module bitwise_xor (
  input  [15:0] in1,
  input  [15:0] in2,
  output [15:0] out
);

  xor xor_1 (out[0], in2[0], in1[0]);
  xor xor_2 (out[1], in2[1], in1[1]);
  xor xor_3 (out[2], in2[2], in1[2]);
  xor xor_4 (out[3], in2[3], in1[3]);
  xor xor_5 (out[4], in2[4], in1[4]);
  xor xor_6 (out[5], in2[5], in1[5]);
  xor xor_7 (out[6], in2[6], in1[6]);
  xor xor_8 (out[7], in2[7], in1[7]);
  xor xor_9 (out[8], in2[8], in1[8]);
  xor xor_10 (out[9], in2[9], in1[9]);
  xor xor_11 (out[10], in2[10], in1[10]);
  xor xor_12 (out[11], in2[11], in1[11]);
  xor xor_13 (out[12], in2[12], in1[12]);
  xor xor_14 (out[13], in2[13], in1[13]);
  xor xor_15 (out[14], in2[14], in1[14]);
  xor xor_16 (out[15], in2[15], in1[15]);
endmodule

// CONTROL
module ControlUnit (
  input  [1:0] in,
  input  clk,
  output imm,
  output PC_plus_plus,
  output IRLD,
  output MUX,
  output LD
);

  wire [1:0] multiplexer_1_out, n2bitreg_1_out;
  wire [23:1] rom_1_data;

  Multiplexer #(.width(2)) multiplexer_1 (
    .in0(in), .in1(2'b00), .out(multiplexer_1_out), .sel(rom_1_data[20]));  // open: en
  _2bitReg u_2bitreg_1 (.in(multiplexer_1_out), .out(n2bitreg_1_out), .load(1'b1), .clk(clk));
  ROM #(.addrWidth(2), .dataWidth(24)) rom_1 (
    .addr(n2bitreg_1_out),
    .data({rom_1_data[23:17], LD, rom_1_data[15:13], MUX, rom_1_data[11:9], IRLD, rom_1_data[7:5], PC_plus_plus, rom_1_data[3:1], imm}));  // open: sel

  // Notes on the sheet:
  //   LOAD
  //   contents of rom_1 (hex, n*v repeats v):
  //   110 111010 110000 110011
  //   FETCH
endmodule

module _2bitReg (
  input  [1:0] in,
  input  load,
  input  clk,
  output [1:0] out
);

  wire and_1_out, and_2_out, and_3_out, and_4_out, not_1_out, not_2_out, s_r_ff_1_qn, s_r_ff_2_qn;

  and and_1 (and_1_out, in[0], load);
  not not_1 (not_1_out, in[0]);
  and and_2 (and_2_out, not_1_out, load);
  and and_3 (and_3_out, in[1], load);
  not not_2 (not_2_out, in[1]);
  and and_4 (and_4_out, not_2_out, load);
  S_R_Flip_Flop s_r_ff_1 (
    .S(and_1_out), .clk(clk), .R(and_2_out), .Q(out[0]), .Qn(s_r_ff_1_qn));  // open: preset, reset, en
  S_R_Flip_Flop s_r_ff_2 (
    .S(and_3_out), .clk(clk), .R(and_4_out), .Q(out[1]), .Qn(s_r_ff_2_qn));  // open: preset, reset, en
endmodule

// PC
module _16bitRegWithInc (
  input  [15:0] datain,
  input  load,
  input  clk,
  input  incr,
  output [15:0] out
);

  wire or_1_out;
  wire [15:0] adder_1_out, multiplexer_1_out;

  Multiplexer #(.width(16)) multiplexer_1 (
    .in0(datain), .in1(adder_1_out), .out(multiplexer_1_out), .sel(incr));  // open: en
  _16bitReg u_16bitreg_1 (.DATAIN(multiplexer_1_out), .LOAD(or_1_out), .CLK(clk), .DATAOUT(out));
  or or_1 (or_1_out, incr, load);
  Adder #(.width(16)) adder_1 (.a(16'h1), .b(out), .out(adder_1_out));  // open: cin, cout
endmodule

module IR (
  input  [11:0] DATAIN,
  input  LOAD,
  input  CLK,
  output [11:0] DATAOUT
);

  wire and_1_out, and_2_out, and_3_out, and_4_out, and_5_out, and_6_out, and_7_out, and_8_out, and_9_out,
       and_10_out, and_11_out, and_12_out, and_13_out, and_14_out, and_15_out, and_16_out, and_17_out,
       and_18_out, and_19_out, and_20_out, and_21_out, and_22_out, and_23_out, and_24_out, not_1_out,
       not_2_out, not_3_out, not_4_out, not_5_out, not_6_out, not_7_out, not_8_out, not_9_out, not_10_out,
       not_11_out, not_12_out, s_r_ff_1_qn, s_r_ff_2_qn, s_r_ff_3_qn, s_r_ff_4_qn, s_r_ff_5_qn, s_r_ff_6_qn,
       s_r_ff_7_qn, s_r_ff_8_qn, s_r_ff_9_qn, s_r_ff_10_qn, s_r_ff_11_qn, s_r_ff_12_qn;

  not not_1 (not_1_out, DATAIN[0]);
  not not_2 (not_2_out, DATAIN[1]);
  not not_3 (not_3_out, DATAIN[2]);
  not not_4 (not_4_out, DATAIN[3]);
  not not_5 (not_5_out, DATAIN[4]);
  not not_6 (not_6_out, DATAIN[5]);
  not not_7 (not_7_out, DATAIN[6]);
  not not_8 (not_8_out, DATAIN[7]);
  not not_9 (not_9_out, DATAIN[8]);
  not not_10 (not_10_out, DATAIN[9]);
  not not_11 (not_11_out, DATAIN[10]);
  not not_12 (not_12_out, DATAIN[11]);
  and and_1 (and_1_out, DATAIN[0], LOAD);
  and and_2 (and_2_out, not_1_out, LOAD);
  and and_3 (and_3_out, DATAIN[1], LOAD);
  and and_4 (and_4_out, not_2_out, LOAD);
  and and_5 (and_5_out, DATAIN[2], LOAD);
  and and_6 (and_6_out, not_3_out, LOAD);
  and and_7 (and_7_out, DATAIN[3], LOAD);
  and and_8 (and_8_out, not_4_out, LOAD);
  and and_9 (and_9_out, DATAIN[4], LOAD);
  and and_10 (and_10_out, not_5_out, LOAD);
  and and_11 (and_11_out, DATAIN[5], LOAD);
  and and_12 (and_12_out, not_6_out, LOAD);
  and and_13 (and_13_out, DATAIN[6], LOAD);
  and and_14 (and_14_out, not_7_out, LOAD);
  and and_15 (and_15_out, DATAIN[7], LOAD);
  and and_16 (and_16_out, not_8_out, LOAD);
  and and_17 (and_17_out, DATAIN[8], LOAD);
  and and_18 (and_18_out, not_9_out, LOAD);
  and and_19 (and_19_out, DATAIN[9], LOAD);
  and and_20 (and_20_out, not_10_out, LOAD);
  and and_21 (and_21_out, DATAIN[10], LOAD);
  and and_22 (and_22_out, not_11_out, LOAD);
  and and_23 (and_23_out, DATAIN[11], LOAD);
  and and_24 (and_24_out, not_12_out, LOAD);
  S_R_Flip_Flop s_r_ff_1 (
    .S(and_1_out), .clk(CLK), .R(and_2_out), .Q(DATAOUT[0]), .Qn(s_r_ff_1_qn));  // open: preset, reset, en
  S_R_Flip_Flop s_r_ff_2 (
    .S(and_3_out), .clk(CLK), .R(and_4_out), .Q(DATAOUT[1]), .Qn(s_r_ff_2_qn));  // open: preset, reset, en
  S_R_Flip_Flop s_r_ff_3 (
    .S(and_5_out), .clk(CLK), .R(and_6_out), .Q(DATAOUT[2]), .Qn(s_r_ff_3_qn));  // open: preset, reset, en
  S_R_Flip_Flop s_r_ff_4 (
    .S(and_7_out), .clk(CLK), .R(and_8_out), .Q(DATAOUT[3]), .Qn(s_r_ff_4_qn));  // open: preset, reset, en
  S_R_Flip_Flop s_r_ff_5 (
    .S(and_9_out), .clk(CLK), .R(and_10_out), .Q(DATAOUT[4]), .Qn(s_r_ff_5_qn));  // open: preset, reset, en
  S_R_Flip_Flop s_r_ff_6 (
    .S(and_11_out), .clk(CLK), .R(and_12_out), .Q(DATAOUT[5]), .Qn(s_r_ff_6_qn));  // open: preset, reset, en
  S_R_Flip_Flop s_r_ff_7 (
    .S(and_13_out), .clk(CLK), .R(and_14_out), .Q(DATAOUT[6]), .Qn(s_r_ff_7_qn));  // open: preset, reset, en
  S_R_Flip_Flop s_r_ff_8 (
    .S(and_15_out), .clk(CLK), .R(and_16_out), .Q(DATAOUT[7]), .Qn(s_r_ff_8_qn));  // open: preset, reset, en
  S_R_Flip_Flop s_r_ff_9 (
    .S(and_17_out), .clk(CLK), .R(and_18_out), .Q(DATAOUT[8]), .Qn(s_r_ff_9_qn));  // open: preset, reset, en
  S_R_Flip_Flop s_r_ff_10 (
    .S(and_19_out), .clk(CLK), .R(and_20_out), .Q(DATAOUT[9]), .Qn(s_r_ff_10_qn));  // open: preset, reset, en
  S_R_Flip_Flop s_r_ff_11 (
    .S(and_21_out), .clk(CLK), .R(and_22_out), .Q(DATAOUT[10]), .Qn(s_r_ff_11_qn));  // open: preset, reset, en
  S_R_Flip_Flop s_r_ff_12 (
    .S(and_23_out), .clk(CLK), .R(and_24_out), .Q(DATAOUT[11]), .Qn(s_r_ff_12_qn));  // open: preset, reset, en
endmodule

module deneme7seg (
  input  [15:0] in_1
);

  Hex_Digit_Display hex_digit_display_1 (.value(in_1[15:12]));  // open: dp
  Hex_Digit_Display hex_digit_display_2 (.value(in_1[11:8]));  // open: dp
  Hex_Digit_Display hex_digit_display_3 (.value(in_1[7:4]));  // open: dp
  Hex_Digit_Display hex_digit_display_4 (.value(in_1[3:0]));  // open: dp
endmodule
